// Logisim project Lab9-Part1.circ as structural Verilog: 3 circuits, main circuit main
module main (
  input  R,
  input  x0,
  input  S,
  input  x1,
  input  x0_2,
  input  s_2,
  input  x1_2,
  input  c_in,
  input  x0_3,
  input  x1_3,
  output Q,
  output Q_prime,
  output y,
  output s_3,
  output s_4,
  output c,
  output c_2
);

  wire and_1_out, and_2_out, and_4_out, and_5_out, not_1_out, xor_2_out;

  not not_1 (not_1_out, s_2);
  and and_1 (and_1_out, x0, not_1_out);
  and and_2 (and_2_out, x1, s_2);
  xor xor_1 (s_4, x0_3, x1_3);
  and and_3 (c_2, x0_3, x1_3);
  or or_1 (y, and_1_out, and_2_out);
  xor xor_2 (xor_2_out, x0_2, x1_2);
  nor nor_1 (Q, R, Q_prime);
  nor nor_2 (Q_prime, Q, ~S);  // NOR_Gate
  xor xor_3 (s_3, xor_2_out, c_in);
  and and_4 (and_4_out, xor_2_out, c_in);
  and and_5 (and_5_out, x0_2, x1_2);
  or or_2 (c, and_4_out, and_5_out);

  // Notes on the sheet:
  //   CSCI 3412, Lab 9
  //   Dongting Cai
  //   2-to-1 multiplexer
  //   1-bit half adder
  //   Part 1
  //   1-bit full adder
  //   SR NOR latch
endmodule

module Part2 (
  input  x0,
  input  c_in,
  input  x1,
  input  x0_2,
  input  y0,
  input  x2,
  input  x3,
  input  s0,
  input  s1,
  input  x1_2,
  input  y1,
  input  D,
  input  E,
  output s0_2,
  output y,
  output s1_2,
  output c,
  output Q,
  output Q_prime
);

  wire and_1_out, and_2_out, and_3_out, and_4_out, and_5_out, and_6_out, and_7_out, and_8_out, and_9_out,
       and_10_out, not_1_out, not_2_out, not_3_out, not_4_out, not_5_out, or_2_out, xor_1_out, xor_2_out;

  not not_1 (not_1_out, s0);
  not not_2 (not_2_out, s1);
  not not_3 (not_3_out, s1);
  not not_4 (not_4_out, s0);
  not not_5 (not_5_out, D);
  and and_1 (and_1_out, x0, not_1_out, not_2_out);
  and and_2 (and_2_out, x1, s0, not_3_out);
  and and_3 (and_3_out, x2, not_4_out, s1);
  and and_4 (and_4_out, x3, s0, s1);
  and and_5 (and_5_out, not_5_out, E);
  and and_6 (and_6_out, E, D);
  nor nor_1 (Q, and_5_out, Q_prime);
  nor nor_2 (Q_prime, Q, and_6_out);
  or or_1 (y, and_1_out, and_2_out, and_3_out, and_4_out);
  xor xor_1 (xor_1_out, x0_2, y0);
  and and_7 (and_7_out, x0_2, y0);
  xor xor_2 (xor_2_out, x1_2, y1);
  and and_8 (and_8_out, x1_2, y1);
  xor xor_3 (s0_2, c_in, xor_1_out);
  and and_9 (and_9_out, xor_1_out, c_in);
  xor xor_4 (s1_2, or_2_out, xor_2_out);
  and and_10 (and_10_out, xor_2_out, or_2_out);
  or or_2 (or_2_out, and_9_out, and_7_out);
  or or_3 (c, and_10_out, and_8_out);

  // Notes on the sheet:
  //   CSCI 3412, Lab 9
  //   Dongting Cai
  //   4-to-1 multiplexer
  //   Gated D latch
  //   Part 2
  //   2-bit full adder
endmodule

module Part3 (
  input  c_in,
  input  x3,
  input  x0,
  input  y3,
  input  y0,
  input  x1,
  input  y1,
  input  x2,
  input  y2,
  output s3,
  output s0,
  output c,
  output s1,
  output s2
);

  wire and_1_out, and_2_out, and_3_out, and_4_out, and_5_out, and_6_out, and_7_out, and_8_out, or_1_out,
       or_2_out, xor_1_out, xor_2_out, xor_5_out, xor_6_out;

  and and_1 (and_1_out, x1, y1);
  xor xor_1 (xor_1_out, x0, y0);
  and and_2 (and_2_out, x0, y0);
  xor xor_2 (xor_2_out, x1, y1);
  xor xor_3 (s0, c_in, xor_1_out);
  and and_3 (and_3_out, xor_1_out, c_in);
  xor xor_4 (s1, or_1_out, xor_2_out);
  and and_4 (and_4_out, xor_2_out, or_1_out);
  or or_1 (or_1_out, and_3_out, and_2_out);
  or or_2 (or_2_out, and_4_out, and_1_out);
  xor xor_5 (xor_5_out, x3, y3);
  and and_5 (and_5_out, x3, y3);
  xor xor_6 (xor_6_out, x2, y2);
  and and_6 (and_6_out, x2, y2);
  xor xor_7 (s3, y3, xor_5_out);
  and and_7 (and_7_out, xor_5_out, y3);
  xor xor_8 (s2, or_2_out, xor_6_out);
  and and_8 (and_8_out, xor_6_out, or_2_out);
  or or_3 (c, and_7_out, and_5_out);
  or or_4 (y3, and_8_out, and_6_out);

  // Notes on the sheet:
  //   CSCI 3412, Lab 9
  //   Dongting Cai
  //   4-bit full adder
  //   Part 3
endmodule
